# Fritzing sketch AgriSensor_Schematics (saved by Fritzing 0.9.6b)
breadboards: 3

parts:
  MH-ET_LIVE_ESP32_DEVKIT1 = MH-ET LIVE ESP32 DEVKIT 38 pins
  T1 = LM34 Temperature Sensor [package="TO92 [THT]"]
  Soil = Soil Moisture Sensor
  ZS-042_RTC1 = ZS-042 RTC Module
  R1 = Resistor [tolerance=±5% power=0.25 resistance=1k package=THT]
  R2 = Resistor [tolerance=±5% power=0.25 resistance=2.2k part_number=2kohms package=THT]
  M1 = ph-4502c [package=THT]
  M2 = MT3608 Module
  Solar_Cell1 = 5V 100mA Polycrystalline PET Solar Cell [part_number=IM130407002]
  Solar_Cell2 = 5V 100mA Polycrystalline PET Solar Cell
  TP1 = TP4056 [chip_label=TP4056 package="DIP (Dual Inline) [THT]"]
  18650_Lithium_Cell = 18650 battery holder [package=battery-18650-kit]
  M3 = MT3608 Module

nets:
  VCC: MH-ET_LIVE_ESP32_DEVKIT1.3V3, T1.+Vs, Soil.VCC, ZS-042_RTC1.VCC, M2.pin2
  N1: MH-ET_LIVE_ESP32_DEVKIT1.IO34, R1.Pin_0, R2.Pin_0
  N2: MH-ET_LIVE_ESP32_DEVKIT1.IO32, Soil.SIG
  GND: MH-ET_LIVE_ESP32_DEVKIT1.GND#58, T1.GND, Soil.GND, ZS-042_RTC1.GND, R2.Pin_1, M2.pin1, M3.pin4
  N3: MH-ET_LIVE_ESP32_DEVKIT1.5V, M3.pin3
  N4: MH-ET_LIVE_ESP32_DEVKIT1.IO22, ZS-042_RTC1.SCL
  N5: MH-ET_LIVE_ESP32_DEVKIT1.IO21, ZS-042_RTC1.SDA
  N6: MH-ET_LIVE_ESP32_DEVKIT1.IO17, T1.Vout
  N7: R1.Pin_1, M1.pin3
  N8: M1.pin5, M2.pin4
  N9: M1.pin6, M2.pin3
  GND_2: Solar_Cell1.GND, Solar_Cell2.GND, TP1.pin2
  5V: Solar_Cell1.5V, Solar_Cell2.5V, TP1.pin1
  N10: TP1.pin3, M3.pin2
  N11: TP1.pin4, 18650_Lithium_Cell.-
  N12: TP1.pin5, 18650_Lithium_Cell.+
  N13: TP1.pin6, M3.pin1

custom parts:
  MH-ET LIVE ESP32 DEVKIT 38 pins: http://mh.nodebb.com/topic/2/mh-et-live-esp32-devkit
  ph-4502c: ph-4502c PH Meter.
  MT3608 Module: MT3608 Boost Converter Module Links: Aerosemi MT3608 2A Step Up Converter datasheet
  5V 100mA Polycrystalline PET Solar Cell: This is 5V 100mA Polycrystalline PET Solar Cell. It is high quality and exquisite appearance. It is used in all kinds of high-grade electronic products.
  TP4056: A DIP stand-in part for whatever IC you want. With 6 pins on a 300mil dual inline package (DIP) footprint.
  18650 battery holder: 18650 Battery
