# Fritzing sketch AgriSensor_Schematics (saved by Fritzing 0.9.10b)
circuit board: 10cm x 10cm
circuit board: 10cm x 20cm
breadboards: 3

parts:
  MH-ET_LIVE_ESP32_DEVKIT1 = MH-ET LIVE ESP32 DEVKIT 38 pins
  BAT1 = 18650 battery holder [package=battery-18650-kit]
  TP1 = TP4056 [chip_label=TP4056 package="DIP (Dual Inline) [THT]"]
  U1 = SWITCH-SPST-2 [package=switch-spst-vertical]
  DC-DC_Step_Up = MT3608 Module
  OLED = Grove OLED 128x96
  ZS-042_RTC1 = ZS-042 RTC Module
  Capacitive_Soil_Moisture_Sensor1 = DFRobot Capacitive Soil Moisture Sensor V1.0 [part_number=SEN0193]
  PH_Sensor = ph-4502c [package=THT]
  M2 = MT3608 Module
  R3 = Resistor [tolerance=±5% power=0.25 resistance=22k package=THT]
  R4 = Resistor [tolerance=±0.05% power=0.25 resistance=33k package=THT]
  R5 = Resistor [tolerance=±0.05% power=0.25 resistance=4.7k package=THT]
  R6 = Resistor [tolerance=±5% power=0.25 resistance=100 package=THT]
  DS2 = DS18B20 1-Wire Temperature Sensor Probe
  JP1 = Header 2 [package=screwterminal-3.5mm-2_lock]  # not connected
  JP2 = Header 2 [package=jst-2-pth]  # not connected
  J2 = JST-B3P-VH [part_number=JST-B3P-VH package=THT]  # not connected
  Input_Capacitor = Electrolytic Capacitor [capacitance=1000μF voltage=50V package="1010 [SMD, electrolytic]"]

nets:
  VCC: MH-ET_LIVE_ESP32_DEVKIT1.3V3, OLED.VCC, ZS-042_RTC1.VCC, Capacitive_Soil_Moisture_Sensor1.VCC, M2.pin2, DS2.VDD
  N1: MH-ET_LIVE_ESP32_DEVKIT1.IO32, Capacitive_Soil_Moisture_Sensor1.A
  GND: MH-ET_LIVE_ESP32_DEVKIT1.GND#58, DC-DC_Step_Up.pin4, OLED.GND, ZS-042_RTC1.GND, Capacitive_Soil_Moisture_Sensor1.GND, M2.pin1, R4.Pin_1, DS2.GND, Input_Capacitor.-
  N2: MH-ET_LIVE_ESP32_DEVKIT1.5V, DC-DC_Step_Up.pin3, Input_Capacitor.+
  N3: MH-ET_LIVE_ESP32_DEVKIT1.IO22, OLED.SCL, ZS-042_RTC1.SCL
  N4: MH-ET_LIVE_ESP32_DEVKIT1.IO21, OLED.SDA, ZS-042_RTC1.SDA
  N5: MH-ET_LIVE_ESP32_DEVKIT1.IO17, R6.Pin_1
  N6: MH-ET_LIVE_ESP32_DEVKIT1.IO16, R3.Pin_1, R4.Pin_0
  N7: BAT1.+, TP1.pin5
  N8: BAT1.-, TP1.pin4
  N9: TP1.pin3, U1.O
  N10: TP1.pin6, DC-DC_Step_Up.pin1
  N11: U1.P, DC-DC_Step_Up.pin2
  N12: PH_Sensor.pin3, R3.Pin_0
  N13: PH_Sensor.pin5, M2.pin4
  N14: PH_Sensor.pin6, M2.pin3
  N15: R5.Pin_0, R6.Pin_0, DS2.DQ

custom parts:
  MH-ET LIVE ESP32 DEVKIT 38 pins: http://mh.nodebb.com/topic/2/mh-et-live-esp32-devkit
  18650 battery holder: 18650 Battery
  TP4056: A DIP stand-in part for whatever IC you want. With 6 pins on a 300mil dual inline package (DIP) footprint.
  MT3608 Module: MT3608 Boost Converter Module Links: Aerosemi MT3608 2A Step Up Converter datasheet
  DFRobot Capacitive Soil Moisture Sensor V1.0: DFRobot Capacitive Soil Moisture Sensor V1.0 This product measures soil moisture levels by capacitive sensing, rather than resistive sensing like other types of moisture sensor. It is made of a corrosion resistant material giving it a long service life. Insert it into soil and impress your friends with the real-time soil moisture data! The product includes an on-board voltage regulator which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
  ph-4502c: ph-4502c PH Meter.
